# Fritzing sketch RoomController (saved by Fritzing 1.0.4)
breadboards: 1

parts:
  A1 = Particle - Photon2
  M1 = BMP280
  S1 = Round Pushbutton
  ZS-042_RTC1 = ZS-042 RTC Module  # not connected
  OLED_I2C1 = OLED 128x64 I2C Monochrome Display
  Part1 = 4x4 Keypad [part_number=101207]

nets:
  VIN: A1.Pin_2, M1.VIN, OLED_I2C1.VDD
  GND: A1.Pin_4, M1.GND, S1.leg0, OLED_I2C1.GND
  N1: A1.Pin_6, Part1.8
  N2: A1.Pin_7, Part1.7
  N3: A1.Pin_10, Part1.5
  N4: A1.Pin_11, Part1.4
  N5: A1.Pin_12, Part1.3
  N6: A1.Pin_15, Part1.1
  N7: A1.Pin_17, M1.SDA, OLED_I2C1.SDA
  N8: A1.Pin_18, M1.SCL, OLED_I2C1.SCK
  N9: A1.Pin_19, S1.leg1

custom parts:
  Particle - Photon2: The Photon 2 is a microcontroller and Wi-Fi networking developed by particle. Features: 802.11a/b/g/n Wi-Fi, 2.4 GHz and 5 GHz Integrated PCB antenna Integrated U.FL connector for external antenna Integrated RF switch BLE 5 using same antenna as Wi-Fi Realtek RTL8721DM MCU ARM Cortex M33 CPU, 200 MHz 2048 KB (2 MB) user application maximum size 3072 KB (3 MB) of RAM available to user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
  BMP280: Temperature Humidity Barometric presure Sensor, I2C
  4x4 Keypad: Matrix membrane keypad 4x4
